# Fritzing sketch Uno_HP-C4280_Enabler (saved by Fritzing 0.8.5b)
breadboards: 2

parts:
  Bauteil3 = Arduino Uno (Rev3)
  Bauteil5 = Arduino Nano (Rev3.0)
  U11 = RELAY-SOLIDSTATE [package=relay-s108t02]
  U12 = RELAY-SOLIDSTATE [package=relay-s108t02]
  U13 = RELAY-SOLIDSTATE [package=relay-s108t02]
  U14 = RELAY-SOLIDSTATE [package=relay-s108t02]
  R1 = Resistor [tolerance=±5% resistance=1k package=THT]
  JP1 = Header 6 [package=molex-1x6-ra_lock]

nets:
  N1: Bauteil3.A0, U14.T2, JP1.2
  N2: Bauteil3.D8, U11.+
  N3: Bauteil3.D9_PWM, U12.+
  N4: Bauteil3.D10_PWM/SS, U13.+
  N5: Bauteil3.D11_PWM/MOSI, U14.+
  5V: Bauteil3.5V, Bauteil5.5V
  GND: Bauteil3.GND, Bauteil5.GND, R1.Pin_1
  N6: U11.T1, U12.T1, U13.T1, JP1.3
  N7: U11.T2, JP1.6
  N8: U11.-, U12.-, U13.-, U14.-, R1.Pin_0
  N9: U12.T2, JP1.5
  N10: U13.T2, JP1.4
  N11: U14.T1, JP1.1
